# Fritzing sketch main (saved by Fritzing 0.9.3b)
breadboards: 1

parts:
  Arduino = Arduino Nano (Rev3.0)
  DHT22 = Humidity and Temperature Sensor RHT03
  BTLE = Bluetooth HC-05 Macho
  Part1 = Adafruit BMP180
  Part2 = Adafruit DS1307 RTC Breakout [part_number="Adafruit #264"]

nets:
  GND: Arduino.GND, DHT22.GND_2, BTLE.GND, Part1.GND, Part2.GND
  N1: Arduino.D2, DHT22.Data-signal
  N2: Arduino.D8, BTLE.TXD
  N3: Arduino.D9, BTLE.RXD
  5V: Arduino.5V, Part2.VCC
  N4: Arduino.A5, Part1.SCL, Part2.SCL
  N5: Arduino.A4, Part1.SDA, Part2.SDA
  VCC: Arduino.3V3, DHT22.Vcc, BTLE.VCC, Part1.+5V

custom parts:
  Adafruit BMP180: This precision sensor from Bosch is the best low-cost sensing solution for measuring barometric pressure and temperature. Because pressure changes with altitude you can also use it as an altimeter! The sensor is soldered onto a PCB with a 3.3V regulator, I2C level shifter and pull-up resistors on the I2C pins. The BMP180 is the next-generation of sensors from Bosch, and replaces the BMP085.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
  Adafruit DS1307 RTC Breakout: This is a great battery-backed real time clock (RTC) that allows your microcontroller project to keep track of time even if it is reprogrammed, or if the power is lost. Perfect for datalogging, clock-building, time stamping, timers and alarms, etc. The DS1307 is the most popular RTC - but it requires 5V power to work (although we've used it with 5V power and 3.3V logic successfully) PCB &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
