# Fritzing sketch main_pcb (saved by Fritzing 0.9.3b)
perfboards: 1

parts:
  Arduino = Arduino Nano (Rev3.0)
  DHT22 = Humidity and Temperature Sensor RHT03
  BTLE = Bluetooth HC-05 Macho
  Part1 = Adafruit BMP180
  Part2 = Adafruit DS1307 RTC Breakout [part_number="Adafruit #264"]
  J2 = female pin header, 4 pins [form="♀ (female)"]
  J4 = female pin header, 4 pins [form="♀ (female)"]
  J8 = female pin header, 1 pin [form="♀ (female)"]
  Part3 = Adafruit I2C+SPI LCD Backpack [part_number="Adafruit #292"]
  J9 = female pin header, 4 pins [form="♀ (female)"]
  J10 = female pin header, 1 pin [form="♀ (female)"]
  J11 = female pin header, 1 pin [form="♀ (female)"]
  J3 = female pin header, 4 pins [form="♀ (female)"]
  J1 = female pin header, 6 pins [form="♀ (female)"]

nets:
  GND: Arduino.GND, DHT22.GND_2, BTLE.GND, Part1.GND, Part2.GND, J2.pin1, J4.pin3, Part3.GND, J9.pin1, J3.pin1, J1.pin3
  N1: Arduino.D2, DHT22.Data-signal, J2.pin3
  N2: Arduino.D8, BTLE.TXD, J1.pin4
  N3: Arduino.D9, BTLE.RXD, J1.pin5
  VCC: Arduino.5V, Part2.VCC, Part3.VCC, J9.pin2, J10.pin1, J3.pin2
  N4: Arduino.A5, Part1.SCL, Part2.SCL, J4.pin2, Part3.DATA, J9.pin4, J11.pin1, J3.pin4
  N5: Arduino.A4, Part1.SDA, Part2.SDA, J4.pin1, J8.pin1, Part3.CLOCK, J9.pin3, J3.pin3
  VCC_2: Arduino.3V3, DHT22.Vcc, BTLE.VCC, Part1.+5V, J2.pin4, J4.pin4, J1.pin2

custom parts:
  Adafruit BMP180: This precision sensor from Bosch is the best low-cost sensing solution for measuring barometric pressure and temperature. Because pressure changes with altitude you can also use it as an altimeter! The sensor is soldered onto a PCB with a 3.3V regulator, I2C level shifter and pull-up resistors on the I2C pins. The BMP180 is the next-generation of sensors from Bosch, and replaces the BMP085.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
  Adafruit DS1307 RTC Breakout: This is a great battery-backed real time clock (RTC) that allows your microcontroller project to keep track of time even if it is reprogrammed, or if the power is lost. Perfect for datalogging, clock-building, time stamping, timers and alarms, etc. The DS1307 is the most popular RTC - but it requires 5V power to work (although we've used it with 5V power and 3.3V logic successfully) PCB &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
  Adafruit I2C+SPI LCD Backpack: LCD backpacks reduce the number of pins needed to connect to an LCD. LCDs are a fun and easy way to have your microcontroller project talk back to you. Character LCDs are common, and easy to get, available in tons of colors and sizes. We've written tutorials on using character LCDs with an Arduino (or similar microcontroller) but find that the number of pins necessary to control the LCD can be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
